// Digital circuit Serial-Parallel_Encoder.dig as structural Verilog
module Serial_Parallel_Encoder (
  input  mi,
  input  clk,
  input  m0,
  input  m1,
  input  m2,
  input  m3,
  input  Clk_2,
  input  LD,
  output Do,
  output Dox,
  output [7:0] Xout
);

  wire not_1_out, not_2_out, not_3_out, not_4_out, not_5_out, not_6_out, not_7_out, not_8_out, not_9_out,
       not_10_out, not_11_out, not_12_out, not_13_out, parenc_0_7_1_x0, parenc_0_7_1_x1, parenc_0_7_1_x2,
       parenc_0_7_1_x3, parenc_0_7_1_x4, parenc_0_7_1_x5, parenc_0_7_1_x6, parenc_0_7_1_x7;

  not not_1 (not_1_out, m0);
  Seven_Seg seven_seg_1 (
    .a(not_1_out), .b(1'b1), .c(1'b1), .d(not_1_out), .e(not_1_out), .f(not_1_out), .g(1'b0), .dp(1'b0));
  not not_2 (not_2_out, m1);
  Seven_Seg seven_seg_2 (
    .a(not_2_out), .b(1'b1), .c(1'b1), .d(not_2_out), .e(not_2_out), .f(not_2_out), .g(1'b0), .dp(1'b0));
  not not_3 (not_3_out, m2);
  Seven_Seg seven_seg_3 (
    .a(not_3_out), .b(1'b1), .c(1'b1), .d(not_3_out), .e(not_3_out), .f(not_3_out), .g(1'b0), .dp(1'b0));
  not not_4 (not_4_out, m3);
  Seven_Seg seven_seg_4 (
    .a(not_4_out), .b(1'b1), .c(1'b1), .d(not_4_out), .e(not_4_out), .f(not_4_out), .g(1'b0), .dp(1'b0));
  ParEnc_0_7 parenc_0_7_1 (
    .m0(m0), .m1(m1), .m2(m2), .m3(m3), .x0(parenc_0_7_1_x0), .x1(parenc_0_7_1_x1), .x2(parenc_0_7_1_x2),
    .x3(parenc_0_7_1_x3), .x4(parenc_0_7_1_x4), .x5(parenc_0_7_1_x5), .x6(parenc_0_7_1_x6),
    .x7(parenc_0_7_1_x7));
  Seven_Seg_Hex seven_seg_hex_1 (.d({m0, m1, m2, m3}), .dp(1'b0));
  not not_5 (not_5_out, Clk_2);
  _74165 _74165_1 (
    .pin1(LD), .pin2(not_5_out), .pin3(1'b1), .pin4(1'b1), .pin5(1'b1), .pin6(1'b0), .pin7(Dox), .pin8(1'b0),
    .pin9(Do), .pin10(1'b0), .pin11(1'b1), .pin12(1'b1), .pin13(1'b1), .pin14(1'b1), .pin15(1'b0),
    .pin16(1'b1));
  // ScopeTrigger #(.maxStepCount(100), .trigger("rising")) scopetrigger_1: pin names not known; wires that end beside it: not_5_out
  Serial_parallel serial_parallel_1 (
    .mi(mi), .Clk(clk), .K0i(parenc_0_7_1_x0), .K1i(parenc_0_7_1_x1), .K2i(parenc_0_7_1_x2),
    .K3i(parenc_0_7_1_x3), .K4i(parenc_0_7_1_x4), .K5i(parenc_0_7_1_x5), .K6i(parenc_0_7_1_x6),
    .k7i(parenc_0_7_1_x7), .x0(Xout[0]), .x1(Xout[1]), .x2(Xout[2]), .x3(Xout[3]), .x4(Xout[4]),
    .x5(Xout[5]), .x6(Xout[6]), .x7(Xout[7]));
  Seven_Seg_Hex seven_seg_hex_2 (.d(Xout[3:0]), .dp(1'b0));
  Seven_Seg_Hex seven_seg_hex_3 (.d(Xout[7:4]), .dp(1'b0));
  Seven_Seg seven_seg_5 (
    .a(not_6_out), .b(1'b1), .c(1'b1), .d(not_6_out), .e(not_6_out), .f(not_6_out), .g(1'b0), .dp(1'b0));
  not not_6 (not_6_out, Xout[0]);
  Seven_Seg seven_seg_6 (
    .a(not_7_out), .b(1'b1), .c(1'b1), .d(not_7_out), .e(not_7_out), .f(not_7_out), .g(1'b0), .dp(1'b0));
  not not_7 (not_7_out, Xout[1]);
  Seven_Seg seven_seg_7 (
    .a(not_8_out), .b(1'b1), .c(1'b1), .d(not_8_out), .e(not_8_out), .f(not_8_out), .g(1'b0), .dp(1'b0));
  not not_8 (not_8_out, Xout[2]);
  Seven_Seg seven_seg_8 (
    .a(not_9_out), .b(1'b1), .c(1'b1), .d(not_9_out), .e(not_9_out), .f(not_9_out), .g(1'b0), .dp(1'b0));
  not not_9 (not_9_out, Xout[3]);
  Seven_Seg seven_seg_9 (
    .a(not_10_out), .b(1'b1), .c(1'b1), .d(not_10_out), .e(not_10_out), .f(not_10_out), .g(1'b0), .dp(1'b0));
  not not_10 (not_10_out, Xout[4]);
  Seven_Seg seven_seg_10 (
    .a(not_11_out), .b(1'b1), .c(1'b1), .d(not_11_out), .e(not_11_out), .f(not_11_out), .g(1'b0), .dp(1'b0));
  not not_11 (not_11_out, Xout[5]);
  Seven_Seg seven_seg_11 (
    .a(not_12_out), .b(1'b1), .c(1'b1), .d(not_12_out), .e(not_12_out), .f(not_12_out), .g(1'b0), .dp(1'b0));
  not not_12 (not_12_out, Xout[6]);
  Seven_Seg seven_seg_12 (
    .a(not_13_out), .b(1'b1), .c(1'b1), .d(not_13_out), .e(not_13_out), .f(not_13_out), .g(1'b0), .dp(1'b0));
  not not_13 (not_13_out, Xout[7]);

  // Notes on the sheet:
  //   mi: default 1
  //   clk: Hz: 2
  //   m1: default 1
  //   m3: default 1
  //   Clk_2: Hz: 16
  //   m'0
  //   m'1
  //   m'2
  //   m'3
endmodule
