// Digital circuit Serial-parallel.dig as structural Verilog
module Serial_parallel (
  input  K0i,
  input  mi,
  input  Clk,
  input  K1i,
  input  K2i,
  input  K3i,
  input  K4i,
  input  K5i,
  input  K6i,
  input  k7i,
  output x0,
  output x1,
  output x2,
  output x3,
  output x4,
  output x5,
  output x6,
  output x7
);

  wire and_1_out, and_2_out, and_3_out, and_4_out, and_5_out, and_6_out, and_7_out, and_8_out, d_ff_1_q,
       d_ff_2_q, d_ff_3_q, d_ff_4_q, d_ff_5_q, d_ff_6_q, d_ff_7_q, d_ff_8_q, d_ff_9_q, xor_1_out, xor_2_out,
       xor_3_out, xor_4_out, xor_5_out, xor_6_out, xor_7_out, xor_8_out;

  D_FF d_ff_1 (.D(mi), .C(Clk), .Q(d_ff_1_q));  // open: nQ
  and and_1 (and_1_out, d_ff_1_q, K0i);
  and and_2 (and_2_out, d_ff_1_q, K1i);
  and and_3 (and_3_out, d_ff_1_q, K2i);
  and and_4 (and_4_out, d_ff_1_q, K3i);
  and and_5 (and_5_out, d_ff_1_q, K4i);
  and and_6 (and_6_out, d_ff_1_q, K5i);
  and and_7 (and_7_out, d_ff_1_q, K6i);
  and and_8 (and_8_out, d_ff_1_q, k7i);
  xor xor_1 (xor_1_out, and_1_out, d_ff_2_q);
  xor xor_2 (xor_2_out, and_2_out, d_ff_3_q);
  xor xor_3 (xor_3_out, and_3_out, d_ff_4_q);
  xor xor_4 (xor_4_out, and_4_out, d_ff_5_q);
  xor xor_5 (xor_5_out, and_5_out, d_ff_6_q);
  xor xor_6 (xor_6_out, and_6_out, d_ff_7_q);
  xor xor_7 (xor_7_out, and_7_out, d_ff_8_q);
  xor xor_8 (xor_8_out, and_8_out, d_ff_9_q);
  D_FF d_ff_2 (.D(xor_1_out), .C(Clk), .Q(d_ff_2_q));  // open: nQ
  D_FF d_ff_3 (.D(xor_2_out), .C(Clk), .Q(d_ff_3_q));  // open: nQ
  D_FF d_ff_4 (.D(xor_3_out), .C(Clk), .Q(d_ff_4_q));  // open: nQ
  D_FF d_ff_5 (.D(xor_4_out), .C(Clk), .Q(d_ff_5_q));  // open: nQ
  D_FF d_ff_6 (.D(xor_5_out), .C(Clk), .Q(d_ff_6_q));  // open: nQ
  D_FF d_ff_7 (.D(xor_6_out), .C(Clk), .Q(d_ff_7_q));  // open: nQ
  D_FF d_ff_8 (.D(xor_7_out), .C(Clk), .Q(d_ff_8_q));  // open: nQ
  D_FF d_ff_9 (.D(xor_8_out), .C(Clk), .Q(d_ff_9_q));  // open: nQ
  D_FF d_ff_10 (.D(d_ff_2_q), .C(Clk), .Q(x0));  // open: nQ
  D_FF d_ff_11 (.D(d_ff_3_q), .C(Clk), .Q(x1));  // open: nQ
  D_FF d_ff_12 (.D(d_ff_4_q), .C(Clk), .Q(x2));  // open: nQ
  D_FF d_ff_13 (.D(d_ff_5_q), .C(Clk), .Q(x3));  // open: nQ
  D_FF d_ff_14 (.D(d_ff_6_q), .C(Clk), .Q(x4));  // open: nQ
  D_FF d_ff_15 (.D(d_ff_7_q), .C(Clk), .Q(x5));  // open: nQ
  D_FF d_ff_16 (.D(d_ff_8_q), .C(Clk), .Q(x6));  // open: nQ
  D_FF d_ff_17 (.D(d_ff_9_q), .C(Clk), .Q(x7));  // open: nQ

  // Notes on the sheet:
  //   K0i: default 1
  //   Clk: Hz: 2
  //   K1i: default 1
  //   K2i: default 1
  //   K3i: default 1
  //   D-FF
endmodule
